# Fritzing sketch Sketch (saved by Fritzing 0.9.3b)
breadboards: 1

parts:
  J1 = STM32 Nucleo boards
  R2 = Resistor [tolerance=±5% resistance=10k package=THT]
  R3 = Photocell (LDR) [package=THT]
  U1 = JOYSTICK-PSP1000 [package=joystick-psp1000]

nets:
  N1: J1.A0, R2.Pin_0, R3.pin_1
  N2: J1.A1, U1.X
  N3: J1.A2, U1.Y
  3V3: J1.3V3, R3.pin_0, U1.VCC
  GND: J1.GND, R2.Pin_1, U1.GND

notes:
  Joystick
  Photocell
  10kΩ
