# Fritzing sketch Sketch (saved by Fritzing 0.9.3b)
breadboards: 1

parts:
  J1 = STM32 Nucleo boards
  X1 = USB Connectors [package=usb-microb]

nets:
  N1: J1.PA11, X1.D-
  N2: J1.PB12, X1.D+
  N3: J1.E5V, X1.VBUS
  N4: J1.JP5_2, J1.JP5_03
  GND: J1.GND, X1.GND

notes:
  Connect to PC with USB cable.
